// Logisim project hw5evolution.circ as structural Verilog: 9 circuits, main circuit MyXOR
module MyXOR (
  input  in_1,
  input  in_2,
  output out_3
);

  wire and_1_out, and_2_out, not_1_out, not_2_out;

  not not_1 (not_1_out, in_1);
  not not_2 (not_2_out, in_2);
  and and_1 (and_1_out, not_1_out, in_2);
  and and_2 (and_2_out, in_1, not_2_out);
  or or_1 (out_3, and_1_out, and_2_out);

  // Notes on the sheet:
  //   Here is a location to build an XOR circuit
  //   You can follow the tutorial (Help menu - "tutorial") or work on your own...
endmodule

module FullAdder (
  input  X,
  input  Y,
  input  CarryIn,
  output Sum,
  output CarryOut
);

  wire a_out, b_out, c_out, d_out, e_out, f_out, g_out, h_out, not_1_out, not_2_out, not_3_out;

  not not_1 (not_1_out, X);
  not not_2 (not_2_out, Y);
  not not_3 (not_3_out, CarryIn);
  and a (a_out, not_1_out, not_2_out, CarryIn);
  and b (b_out, not_1_out, Y, not_3_out);
  and c (c_out, X, not_2_out, not_3_out);
  and d (d_out, X, Y, CarryIn);
  and e (e_out, not_1_out, Y, CarryIn);
  and f (f_out, X, not_2_out, CarryIn);
  and g (g_out, X, Y, not_3_out);
  and h (h_out, X, Y, CarryIn);
  or or_1 (Sum, a_out, b_out, c_out, d_out);
  or or_2 (CarryOut, e_out, f_out, g_out, h_out);

  // Notes on the sheet:
  //   3 input bits:  X,  Y,  and CarryIn
  //   Here is a location to build an FULL ADDER circuit
  //   (1) draw the other four rails   (2) you'll need 8 AND gates    (3)  you'll need 2 OR gates
  //   two output bits:  Sum and CarryOut
endmodule

module A_4bit_Ripple_Carry_Adder (
  input  Y3,
  input  Y2,
  input  Y1,
  input  Y0,
  input  X3,
  input  X2,
  input  X1,
  input  X0,
  output Sum4,
  output Sum3,
  output Sum2,
  output Sum1,
  output Sum0
);

  wire fulladder_2_carryout, fulladder_3_carryout, fulladder_4_carryout;

  FullAdder fulladder_1 (.X(Y3), .Y(X3), .CarryIn(fulladder_2_carryout), .Sum(Sum3), .CarryOut(Sum4));
  FullAdder fulladder_2 (.X(Y2), .Y(X2), .CarryIn(fulladder_3_carryout), .Sum(Sum2), .CarryOut(fulladder_2_carryout));
  FullAdder fulladder_3 (.X(Y1), .Y(X1), .CarryIn(fulladder_4_carryout), .Sum(Sum1), .CarryOut(fulladder_3_carryout));
  FullAdder fulladder_4 (.X(Y0), .Y(X0), .CarryIn(1'b0), .Sum(Sum0), .CarryOut(fulladder_4_carryout));

  // Notes on the sheet:
  //   Here is a location to build an 4-bit RIPPLE-CARRY ADDER circuit
  //   8 input bits
  //   5 output bits
endmodule

module A_4bit_Multiplier (
  input  Y3,
  input  Y2,
  input  Y1,
  input  Y0,
  input  X3,
  input  X2,
  input  X1,
  input  X0,
  output Z7,
  output Z6,
  output Z5,
  output Z4,
  output Z3,
  output Z2,
  output Z1,
  output Z0
);


  // Notes on the sheet:
  //   factor (4 bits)
  //   See the problem for details on this hint:   Build a 4x1-bit multiplier first!
  //   second factor (4 bits)
  //   product (8 bits)
  //   4-bit MULTIPLIER circuit
  //   most significant (highest) output bit
  //   least significant (lowest) output bit
endmodule

module A_3by2_divider (
  input  Y2,
  input  Y1,
  input  Y0,
  input  X1,
  input  X0,
  output Z2,
  output Z1,
  output Z0,
  output Error
);


  // Notes on the sheet:
  //   Dividend (3 bits: Y2 Y1 Y0)
  //   Divisor (2 bits: X1 X0)
  //   Quotient (4 bits: Z2 Z1 Z0 and Error)
  //   3-by-2-bit DIVIDER circuit
endmodule

module A_2bit_decoder (
  input  Input0,
  input  Input1,
  output Output0,
  output Output1,
  output Output2,
  output Output3
);

  wire not_1_out, not_2_out;

  not not_1 (not_1_out, Input0);
  not not_2 (not_2_out, Input1);
  and and_1 (Output0, not_1_out, not_2_out);
  and and_2 (Output1, not_1_out, Input1);
  and and_3 (Output2, Input0, not_2_out);
  and and_4 (Output3, Input0, Input1);

  // Notes on the sheet:
  //   2-bit DECODER circuit (extra credit - see hw)
endmodule

module A_12nGb_memory (
  input  D1,
  input  D2,
  input  D3,
  input  A1,
  input  A2,
  input  Write,
  input  Read,
  output O1,
  output O2,
  output O3
);

  wire a_2bit_decoder_1_output0, a_2bit_decoder_1_output1, a_2bit_decoder_1_output2,
       a_2bit_decoder_1_output3, and_1_out, and_2_out, and_3_out, and_4_out, and_5_out, and_6_out, and_7_out,
       and_8_out, and_9_out, and_10_out, and_11_out, and_12_out, and_13_out, and_14_out, and_15_out,
       and_16_out, and_17_out, and_18_out, and_19_out, and_20_out, d_gate_1_q, d_gate_2_q, d_gate_3_q,
       d_gate_4_q, d_gate_5_q, d_gate_6_q, d_gate_7_q, d_gate_8_q, d_gate_9_q, d_gate_10_q, d_gate_11_q,
       d_gate_12_q;

  A_2bit_decoder a_2bit_decoder_1 (
    .Input0(A1), .Input1(A2), .Output0(a_2bit_decoder_1_output0), .Output1(a_2bit_decoder_1_output1),
    .Output2(a_2bit_decoder_1_output2), .Output3(a_2bit_decoder_1_output3));
  and and_1 (and_1_out, Write, a_2bit_decoder_1_output0);
  and and_2 (and_2_out, Write, a_2bit_decoder_1_output1);
  and and_3 (and_3_out, Write, a_2bit_decoder_1_output2);
  and and_4 (and_4_out, Write, a_2bit_decoder_1_output3);
  buf and_5 (and_5_out, a_2bit_decoder_1_output0);  // AND_Gate
  buf and_6 (and_6_out, a_2bit_decoder_1_output1);  // AND_Gate
  buf and_7 (and_7_out, a_2bit_decoder_1_output2);  // AND_Gate
  buf and_8 (and_8_out, a_2bit_decoder_1_output3);  // AND_Gate
  D_Gate d_gate_1 (.Data(D1), .Enable(and_1_out), .Q(d_gate_1_q));
  D_Gate d_gate_2 (.Data(D1), .Enable(and_2_out), .Q(d_gate_2_q));
  D_Gate d_gate_3 (.Data(D1), .Enable(and_3_out), .Q(d_gate_3_q));
  D_Gate d_gate_4 (.Data(D1), .Enable(and_4_out), .Q(d_gate_4_q));
  and and_9 (and_9_out, d_gate_1_q, and_5_out);
  and and_10 (and_10_out, d_gate_2_q, and_6_out);
  and and_11 (and_11_out, d_gate_3_q, and_7_out);
  and and_12 (and_12_out, d_gate_4_q, and_8_out);
  or or_1 (O1, and_9_out, and_10_out, and_11_out, and_12_out);
  D_Gate d_gate_5 (.Data(D2), .Enable(and_1_out), .Q(d_gate_5_q));
  D_Gate d_gate_6 (.Data(D2), .Enable(and_2_out), .Q(d_gate_6_q));
  D_Gate d_gate_7 (.Data(D2), .Enable(and_3_out), .Q(d_gate_7_q));
  D_Gate d_gate_8 (.Data(D2), .Enable(and_4_out), .Q(d_gate_8_q));
  and and_13 (and_13_out, d_gate_5_q, and_5_out);
  and and_14 (and_14_out, d_gate_6_q, and_6_out);
  and and_15 (and_15_out, d_gate_7_q, and_7_out);
  and and_16 (and_16_out, d_gate_8_q, and_8_out);
  or or_2 (O2, and_13_out, and_14_out, and_15_out, and_16_out);
  D_Gate d_gate_9 (.Data(D3), .Enable(and_1_out), .Q(d_gate_9_q));
  D_Gate d_gate_10 (.Data(D3), .Enable(and_2_out), .Q(d_gate_10_q));
  D_Gate d_gate_11 (.Data(D3), .Enable(and_3_out), .Q(d_gate_11_q));
  D_Gate d_gate_12 (.Data(D3), .Enable(and_4_out), .Q(d_gate_12_q));
  and and_17 (and_17_out, d_gate_9_q, and_5_out);
  and and_18 (and_18_out, d_gate_10_q, and_6_out);
  and and_19 (and_19_out, d_gate_11_q, and_7_out);
  and and_20 (and_20_out, d_gate_12_q, and_8_out);
  or or_3 (O3, and_17_out, and_18_out, and_19_out, and_20_out);

  // Notes on the sheet:
  //   12 nanogigabit MEMORY circuit (extra credit - see hw)
endmodule

module SR_Latch (
  input  R,
  input  S,
  output out_3,
  output out_4
);

  nor nor_1 (out_3, R, out_4);
  nor nor_2 (out_4, out_3, S);
endmodule

module D_Gate (
  input  Data,
  input  Enable,
  output Q
);

  wire and_1_out, and_2_out, not_1_out, not_2_out;

  not not_1 (not_1_out, Data);
  not not_2 (not_2_out, Enable);
  and and_1 (and_1_out, Data, Enable);
  and and_2 (and_2_out, not_1_out, Enable);
  SR_Latch sr_latch_1 (.R(and_2_out), .S(and_1_out), .out_3(Q));  // open: out_4
endmodule
